# Fritzing sketch Laser Mouse Control (saved by Fritzing 0.7.10b)
breadboards: 1

parts:
  Arduino1 = Arduino
  ADNS-9800 = mystery part, 8 pins [chip_label=?]
  LCD1 = LCD screen
  R1 = Rotary Potentiometer (Large) [maximum_resistance=20k package=THT]
  R2 = 15 Ω Resistor [package=THT]

nets:
  N1: Arduino1.D13, ADNS-9800.pin3
  N2: Arduino1.D12, ADNS-9800.pin4
  N3: Arduino1.D11, ADNS-9800.pin2
  N4: Arduino1.D10, ADNS-9800.pin1
  N5: Arduino1.D9, LCD1.RS
  N6: Arduino1.D8, LCD1.E
  N7: Arduino1.D7, LCD1.DB4
  N8: Arduino1.D6, LCD1.DB5
  N9: Arduino1.D5, LCD1.DB6
  N10: Arduino1.D4, LCD1.DB7
  N11: Arduino1.D2, ADNS-9800.pin8
  N12: Arduino1.+5V, ADNS-9800.pin5, R1.leg2, R2.Pin_1
  N13: Arduino1.GND, ADNS-9800.pin6, ADNS-9800.pin7, LCD1.R/W, R1.leg1
  N14: LCD1.VSS, LCD1.LED-
  N15: LCD1.V0, R1.wiper
  N16: LCD1.LED+, R2.Pin_0

notes:
  ADNS-9800 Pins:
  SS|MO|SC|MI|VI|AG|DG|MOT
  ______________________________________________________________
  |ADNS-9800 | Arduino |
  |SS | 10 |
  |MO | 11 |
  |SC | 13 |
  |MI | 12 |
  |MOT | 2 |
  |VI |+5V (First You must Activate 5V Mode) |
  |AG | Gnd |
  |DG | Gnd |
  ______________________________________________________________
